# Fritzing sketch TOFsensorDesign (saved by Fritzing 0.9.3b)
circuit board: 2.03208cm x 1.56878cm
breadboards: 1

parts:
  Part1 = Adafruit VL53L0X Time of Flight Distance Sensor [part_number="Adafruit #3317"]
  J2 = female pin header, 2 pins [form="♀ (female)"]
  J1 = female pin header, 2 pins [form="♀ (female)"]

nets:
  N1: Part1.VIN, Part1.XSHUT, J1.pin2
  N2: Part1.GND, J1.pin1
  N3: Part1.SCL, J2.pin1
  N4: Part1.SDA, J2.pin2

custom parts:
  Adafruit VL53L0X Time of Flight Distance Sensor: The VL53L0X is a Time of Flight distance sensor like no other you've used! The sensor contains a very tiny invisible laser source, and a matching sensor. The VL53L0X can detect the "time of flight", or how long the light has taken to bounce back to the sensor. Since it uses a very narrow light source, it is good for determining distance of only the surface directly in front of it. Unlike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
